// Logisim project code.circ as structural Verilog: 1 circuit, main circuit main
module main (
  input  A,
  input  B,
  input  C,
  input  D
);

  wire B_nCD_out, B_nD_out, BD_out, C_nD_out, CD_out, D0_out, D1_out, D2_out, D3_out, D4_out, D5_out, D6_out,
       nB_nD_out, nBC_out, nC_nD_out, nCB_out, not_1_out, not_2_out, not_3_out;

  not not_1 (not_1_out, B);
  not not_2 (not_2_out, C);
  not not_3 (not_3_out, D);
  and B_nCD (B_nCD_out, B, not_2_out, D);
  and nB_nD (nB_nD_out, not_1_out, not_3_out);
  and nBC (nBC_out, not_1_out, C);
  and C_nD (C_nD_out, not_3_out, C);
  and nCB (nCB_out, B, not_2_out);
  and CD (CD_out, C, D);
  and nC_nD (nC_nD_out, not_2_out, not_3_out);
  and B_nD (B_nD_out, B, not_3_out);
  and BD (BD_out, B, D);
  or D0 (D0_out, A, B_nCD_out, nB_nD_out, nBC_out, C_nD_out);
  or D1 (D1_out, D, not_2_out, B);
  or D2 (D2_out, C_nD_out, nB_nD_out);
  or D3 (D3_out, nCB_out, A, C_nD_out, nBC_out);
  or D4 (D4_out, CD_out, not_1_out, nC_nD_out);
  or D5 (D5_out, A, nC_nD_out, nCB_out, B_nD_out);
  or D6 (D6_out, A, C, BD_out, nB_nD_out);
  _7_Segment_Display u_7_segment_display_1 (
    .g(D3_out), .f(D5_out), .a(D6_out), .b(D4_out), .e(D2_out), .d(D0_out), .c(D1_out));  // open: dp

  // Notes on the sheet:
  //   VẼ đèn led 7 đoạn
endmodule
